# Fritzing sketch schematic (saved by Fritzing 0.7.10b)
breadboards: 1

parts:
  U1 = atmega328 [package=dip]
  S1 = Pushbutton [package="[THT]"]
  D1 = Rectifier Diode [part_number=1N4001 package="300 mil [THT]"]
  R1 = Resistor [tolerance=±5% resistance=10 package=THT]
  R2 = Resistor [tolerance=±5% resistance=10 package=THT]
  R3 = Resistor [tolerance=±5% resistance=10 package=THT]
  R4 = Resistor [tolerance=±5% resistance=10 package=THT]
  IC1 = Single-Chip USB to UART Bridge [package=mlp28]  # not connected
  LED2 = LED - 5mm [color="Yellow (595nm)" package="5 mm [THT]"]
  LED5 = LED - 5mm [color="Red (660nm)" package="5 mm [THT]"]
  LED6 = LED - 5mm [color="Green (570nm)" package="5 mm [THT]"]
  LED7 = LED - 5mm [color="Yellow (595nm)" package="5 mm [THT]"]
  LED8 = LED - 3mm [color="White (4500K)" package="3 mm [THT]"]
  C1 = Ceramic Capacitor [capacitance=100nF package="100 mil [THT, multilayer]"]
  R5 = Resistor [tolerance=±5% resistance=220 package=THT]
  XTAL1 = Crystal [frequency="16 Mhz" package=THT]
  C2 = Ceramic Capacitor [capacitance=22µF package="100 mil [THT, multilayer]"]
  C3 = Ceramic Capacitor [capacitance=22µF package="100 mil [THT, multilayer]"]
  C4 = Ceramic Capacitor [capacitance=100nF package="100 mil [THT, multilayer]"]
  C5 = Ceramic Capacitor [capacitance=100nF package="100 mil [THT, multilayer]"]
  C6 = Ceramic Capacitor [capacitance=100nF package="100 mil [THT, multilayer]"]
  C7 = Electrolytic Capacitor [capacitance=10µF package="100 mil [THT, electrolytic]"]
  VCC1 = 4 x AAA Battery Mount

nets:
  N1: U1.RESET, U1.D2, S1.Pin_1, S1.Pin_2, D1.anode, C1.1, R5.Pin_0
  N2: U1.VCC, U1.AVCC, D1.cathode, R5.Pin_1, C4.0, C6.1, C7.+
  N3: U1.GND, S1.Pin_3, S1.Pin_4, R1.Pin_1, R2.Pin_1, R3.Pin_1, R4.Pin_1, LED2.cathode, LED5.cathode, LED6.cathode, LED7.cathode, LED8.cathode, C4.1, C5.0, C6.0, C7.-, VCC1.+
  N4: U1.XLAT1, C3.0, VCC1.-
  N5: U1.XLAT2, XTAL1.pin_1, C2.0, C3.1
  N6: U1.D5_(PWM), XTAL1.pin_0, C2.1
  N7: U1.D9_(PWM), LED5.anode
  N8: U1.D10_(PWM), LED6.anode
  N9: U1.D11_(PWM), LED2.anode
  N10: U1.D12, LED7.anode
  N11: U1.D13, LED8.anode
  N12: U1.AREF, C5.1
  N13: U1.A0, R4.Pin_0
  N14: U1.A2, R3.Pin_0
  N15: U1.A3, R2.Pin_0
  N16: U1.A5, R1.Pin_0
